// Digital circuit CPU.dig as structural Verilog
module CPU (
  input  clear,
  input  clk
);

  wire and_1_out, and_2_out, beq, bgt, bgt_p3, bgt_p32, bgt_p33, bgt_p41, bgt_p42, bgt_p43, bgt_p44, bgt_p45,
       bgt_p46, bgt_p47, bgt_p48, bgt_p49, bgt_p50, bgt_p51, bgt_p52, bgt_p53, bgt_p54, bgt_p55, bgt_p56,
       bgt_p57, bgt_p58, bgte, blt, blte, bne, id_ex_1_abs_rel_branch_jal_r_2, id_ex_1_adc_2, id_ex_1_add_2,
       id_ex_1_and_2, id_ex_1_asr_2, id_ex_1_beq_2, id_ex_1_bgt_2, id_ex_1_bgte_2, id_ex_1_blt_2,
       id_ex_1_blte_2, id_ex_1_bne_2, id_ex_1_branch_2, id_ex_1_cmp_2, id_ex_1_div_2, id_ex_1_divs_2,
       id_ex_1_jal_r_2, id_ex_1_jalorjjalr, id_ex_1_jmp_2, id_ex_1_lbs_2, id_ex_1_lbu_2, id_ex_1_limm_2,
       id_ex_1_lsl_2, id_ex_1_lsr_2, id_ex_1_lw_2, id_ex_1_mul_2, id_ex_1_muls_2, id_ex_1_nor_2,
       id_ex_1_sb_2, id_ex_1_sub_2, id_ex_1_sw_2, id_ex_1_xnor_2, id_ex_1_xor_2,
       instruction_decoder_1_abs_rel, instruction_decoder_1_adc, instruction_decoder_1_add,
       instruction_decoder_1_and, instruction_decoder_1_asr, instruction_decoder_1_beq,
       instruction_decoder_1_bgt, instruction_decoder_1_bgte, instruction_decoder_1_blt,
       instruction_decoder_1_blte, instruction_decoder_1_bne, instruction_decoder_1_branch,
       instruction_decoder_1_cmp, instruction_decoder_1_div, instruction_decoder_1_divs,
       instruction_decoder_1_jal_r, instruction_decoder_1_jalorjalr, instruction_decoder_1_jmp,
       instruction_decoder_1_lbs, instruction_decoder_1_lbu, instruction_decoder_1_limm,
       instruction_decoder_1_lsl, instruction_decoder_1_lsr, instruction_decoder_1_lw,
       instruction_decoder_1_mul, instruction_decoder_1_muls, instruction_decoder_1_nor,
       instruction_decoder_1_sb, instruction_decoder_1_sub, instruction_decoder_1_sw,
       instruction_decoder_1_xnor, instruction_decoder_1_xor, jmp, multiplexer_1_out, multiplexer_2_out,
       not_1_out, or_1_out, or_2_out, or_3_out, or_4_out, or_5_out, or_6_out, or_7_out, or_8_out, or_9_out,
       riiscv1_1_p1, riiscv1_1_p2, riiscv1_1_p15, riiscv1_1_p16, riiscv1_1_p17, undriven, undriven_2,
       undriven_3, undriven_4, xor_1_out, xor_2_out, xor_3_out, xor_4_out, xor_5_out, xor_6_out;
  wire [4:0] id_ex_1_shft_amt_2, instruction_decoder_1_rd, instruction_decoder_1_rs1,
       instruction_decoder_1_rs2, instruction_decoder_1_rs3, instruction_decoder_1_shft_amt_5bit, rd_q,
       rs1_q, rs2_q, rs3_q;
  wire [15:0] add_1_s, d_ff_as_1_q, id_ex_1_imm_2, instruction_decoder_1_imm_16bit, multiplexer_3_out,
       PC_plus_1_2_q, PC_plus_1_q, riiscv1_1_p18, rs1_2_q, rs4_q, shft_1_p6, shft_1_p7, triportregs_1_src1,
       triportregs_1_src2, triportregs_1_src3, undriven_5;
  wire [31:0] PROM_d;

  D_FF_AS #(.Bits(16)) d_ff_as_1 (
    .Set(1'b0), .D(undriven_5), .C(undriven_4), .Clr(undriven_3), .Q(d_ff_as_1_q));  // open: nQ
  ROM #(.AddrBits(16), .isProgramMemory("true"), .Bits(32)) PROM (.A(d_ff_as_1_q), .D(PROM_d));  // open: sel
  Add #(.Bits(16)) add_1 (.a(d_ff_as_1_q), .b({16{1'b0}}), .c_i(1'b1), .s(add_1_s));  // open: c_o
  Instruction_Decoder instruction_decoder_1 (
    .Instruction(PROM_d), .rd(instruction_decoder_1_rd), .rs1(instruction_decoder_1_rs1),
    .imm_16bit(instruction_decoder_1_imm_16bit), .shft_amt_5bit(instruction_decoder_1_shft_amt_5bit),
    .rs2(instruction_decoder_1_rs2), .rs3(instruction_decoder_1_rs3),
    .abs_rel(instruction_decoder_1_abs_rel), .jmp(instruction_decoder_1_jmp),
    .bgt(instruction_decoder_1_bgt), .bgte(instruction_decoder_1_bgte), .beq(instruction_decoder_1_beq),
    .blte(instruction_decoder_1_blte), .blt(instruction_decoder_1_blt), .bne(instruction_decoder_1_bne),
    .JALorJALR(instruction_decoder_1_jalorjalr), .add(instruction_decoder_1_add),
    .sub(instruction_decoder_1_sub), .adc(instruction_decoder_1_adc), .cmp(instruction_decoder_1_cmp),
    .\nor (instruction_decoder_1_nor), .\and (instruction_decoder_1_and), .\xor (instruction_decoder_1_xor),
    .\xnor (instruction_decoder_1_xnor), .lsl(instruction_decoder_1_lsl), .lsr(instruction_decoder_1_lsr),
    .asr(instruction_decoder_1_asr), .lbu(instruction_decoder_1_lbu), .lbs(instruction_decoder_1_lbs),
    .lw(instruction_decoder_1_lw), .sw(instruction_decoder_1_sw), .limm(instruction_decoder_1_limm),
    .mul(instruction_decoder_1_mul), .muls(instruction_decoder_1_muls), .div(instruction_decoder_1_div),
    .divs(instruction_decoder_1_divs), .branch(instruction_decoder_1_branch),
    .jal_r(instruction_decoder_1_jal_r), .sb(instruction_decoder_1_sb));
  D_FF_AS #(.Bits(5)) rd (.Set(1'b0), .D(instruction_decoder_1_rd), .C(clk), .Clr(clear), .Q(rd_q));  // open: nQ
  D_FF_AS #(.Bits(5)) rs1 (.Set(1'b0), .D(instruction_decoder_1_rs1), .C(clk), .Clr(clear), .Q(rs1_q));  // open: nQ
  D_FF_AS #(.Bits(5)) rs2 (.Set(1'b0), .D(instruction_decoder_1_rs2), .C(clk), .Clr(clear), .Q(rs2_q));  // open: nQ
  D_FF_AS #(.Bits(5)) rs3 (.Set(1'b0), .D(instruction_decoder_1_rs3), .C(clk), .Clr(clear), .Q(rs3_q));  // open: nQ
  ID_EX id_ex_1 (
    .shft_amt(instruction_decoder_1_shft_amt_5bit), .imm(instruction_decoder_1_imm_16bit),
    .abs_rel_branch_jal_r(instruction_decoder_1_abs_rel), .jmp(instruction_decoder_1_jmp),
    .bgt(instruction_decoder_1_bgt), .bgte(instruction_decoder_1_bgte), .beq(instruction_decoder_1_beq),
    .blte(instruction_decoder_1_blte), .blt(instruction_decoder_1_blt), .bne(instruction_decoder_1_bne),
    .JALorJALR(instruction_decoder_1_jalorjalr), .add(instruction_decoder_1_add),
    .sub(instruction_decoder_1_sub), .adc(instruction_decoder_1_adc), .cmp(instruction_decoder_1_cmp),
    .\nor (instruction_decoder_1_nor), .\and (instruction_decoder_1_and), .\xor (instruction_decoder_1_xor),
    .\xnor (instruction_decoder_1_xnor), .lsl(instruction_decoder_1_lsl), .lsr(instruction_decoder_1_lsr),
    .asr(instruction_decoder_1_asr), .lbu(instruction_decoder_1_lbu), .lbs(instruction_decoder_1_lbs),
    .lw(instruction_decoder_1_lw), .sw(instruction_decoder_1_sw), .sb(instruction_decoder_1_sb),
    .limm(instruction_decoder_1_limm), .mul(instruction_decoder_1_mul), .muls(instruction_decoder_1_muls),
    .div(instruction_decoder_1_div), .divs(instruction_decoder_1_divs),
    .branch(instruction_decoder_1_branch), .jal_r(instruction_decoder_1_jal_r), .clear(clear), .clk(clk),
    .shft_amt_2(id_ex_1_shft_amt_2), .imm_2(id_ex_1_imm_2),
    .abs_rel_branch_jal_r_2(id_ex_1_abs_rel_branch_jal_r_2), .jmp_2(id_ex_1_jmp_2), .bgt_2(id_ex_1_bgt_2),
    .bgte_2(id_ex_1_bgte_2), .beq_2(id_ex_1_beq_2), .blte_2(id_ex_1_blte_2), .blt_2(id_ex_1_blt_2),
    .bne_2(id_ex_1_bne_2), .JALorJJALR(id_ex_1_jalorjjalr), .add_2(id_ex_1_add_2), .sub_2(id_ex_1_sub_2),
    .adc_2(id_ex_1_adc_2), .cmp_2(id_ex_1_cmp_2), .nor_2(id_ex_1_nor_2), .and_2(id_ex_1_and_2),
    .xor_2(id_ex_1_xor_2), .xnor_2(id_ex_1_xnor_2), .lsl_2(id_ex_1_lsl_2), .lsr_2(id_ex_1_lsr_2),
    .asr_2(id_ex_1_asr_2), .lbu_2(id_ex_1_lbu_2), .lbs_2(id_ex_1_lbs_2), .lw_2(id_ex_1_lw_2),
    .sw_2(id_ex_1_sw_2), .sb_2(id_ex_1_sb_2), .limm_2(id_ex_1_limm_2), .mul_2(id_ex_1_mul_2),
    .muls_2(id_ex_1_muls_2), .div_2(id_ex_1_div_2), .divs_2(id_ex_1_divs_2), .branch_2(id_ex_1_branch_2),
    .jal_r_2(id_ex_1_jal_r_2));
  D_FF_AS #(.Bits(16)) PC_plus_1 (.Set(1'b0), .D(add_1_s), .C(clk), .Clr(clear), .Q(PC_plus_1_q));  // open: nQ
  or or_1 (or_1_out, multiplexer_1_out, multiplexer_2_out);
  Multiplexer multiplexer_1 (.sel(undriven), .out(multiplexer_1_out));  // open: in_0, in_1
  Multiplexer multiplexer_2 (.sel(undriven_2), .out(multiplexer_2_out));  // open: in_0, in_1
  TRIportRegs triportregs_1 (
    .src1addr(rs1_q), .src2addr(rs2_q), .src3addr(rs3_q), .waddr(rd_q), .src1(triportregs_1_src1),
    .src2(triportregs_1_src2), .src3(triportregs_1_src3));  // open: saved_temp_index_and_pointer, mhdata, mldata, dqdata, drdata, muldivclock, s_t_i_p_clock
  D_FF_AS #(.Bits(16)) rs1_2 (.D(triportregs_1_src1), .C(clk), .Clr(clear), .Q(rs1_2_q));  // open: Set, nQ
  D_FF_AS #(.Bits(16)) rs4 (.D(triportregs_1_src2), .C(clk), .Clr(clear), .Q(rs4_q));  // open: Set, nQ
  D_FF_AS #(.Bits(16)) rs3_2 (.D(triportregs_1_src3), .C(clk), .Clr(clear));  // open: Set, Q, nQ
  // ID_EX bgt: pin names not known; wires that end beside it: id_ex_1_shft_amt_2, id_ex_1_imm_2, bgt_p3, id_ex_1_jmp_2, id_ex_1_bgt_2, id_ex_1_bgte_2, id_ex_1_beq_2, id_ex_1_blte_2, id_ex_1_blt_2, id_ex_1_bne_2, id_ex_1_jalorjjalr, id_ex_1_add_2, id_ex_1_sub_2, id_ex_1_adc_2, id_ex_1_cmp_2, id_ex_1_nor_2, id_ex_1_and_2, id_ex_1_xor_2, id_ex_1_xnor_2, id_ex_1_lsl_2, id_ex_1_lsr_2, id_ex_1_asr_2, id_ex_1_lbu_2, id_ex_1_lbs_2, id_ex_1_lw_2, id_ex_1_sw_2, id_ex_1_sb_2, id_ex_1_limm_2, id_ex_1_mul_2, id_ex_1_muls_2, id_ex_1_div_2, bgt_p32, bgt_p33, jmp, bgt, bgte, beq, blte, blt, bne, bgt_p41, bgt_p42, bgt_p43, bgt_p44, bgt_p45, bgt_p46, bgt_p47, bgt_p48, bgt_p49, bgt_p50, bgt_p51, bgt_p52, bgt_p53, bgt_p54, bgt_p55, bgt_p56, bgt_p57, bgt_p58, bgt_p41
  D_FF_AS #(.Bits(16)) PC_plus_1_2 (.Set(1'b0), .D(PC_plus_1_q), .C(clk), .Clr(clear), .Q(PC_plus_1_2_q));  // open: nQ
  or or_2 (or_2_out, bgt_p33, rs4_q[0]);
  and and_1 (and_1_out, riiscv1_1_p1, bgt_p45);
  or or_3 (or_3_out, bgt_p43, bgt_p42, bgt_p44);
  and and_2 (and_2_out, riiscv1_1_p2, or_3_out);
  or or_4 (or_4_out, bgt_p43, bgt_p45);
  // riiscv1 riiscv1_1: pin names not known; wires that end beside it: riiscv1_1_p1, riiscv1_1_p2, and_2_out, and_1_out, rs1_2_q, or_2_out, 1'b0, bgt_p49, bgt_p48, bgt_p46, bgt_p47, or_4_out, bgt_p42, bgt_p44, riiscv1_1_p15, riiscv1_1_p16, riiscv1_1_p17, riiscv1_1_p18
  xor xor_1 (xor_1_out, beq, riiscv1_1_p16);
  xor xor_2 (xor_2_out, blt, riiscv1_1_p15);
  xor xor_3 (xor_3_out, blte, or_5_out);
  or or_5 (or_5_out, riiscv1_1_p15, riiscv1_1_p16);
  or or_6 (or_6_out, riiscv1_1_p16, riiscv1_1_p17);
  xor xor_4 (xor_4_out, or_6_out, bgte);
  xor xor_5 (xor_5_out, riiscv1_1_p17, bgt);
  not not_1 (not_1_out, riiscv1_1_p16);
  xor xor_6 (xor_6_out, not_1_out, bne);
  or or_7 (or_7_out, xor_1_out, jmp, xor_2_out, xor_3_out, xor_4_out, xor_5_out, xor_6_out);
  or or_8 (or_8_out, rs4_q[0], bgt_p32);
  Multiplexer #(.Bits(16)) multiplexer_3 (
    .sel(or_3_out), .in_0({16{1'b0}}), .in_1(riiscv1_1_p18), .out(multiplexer_3_out));
  // shft shft_1: pin names not known; wires that end beside it: rs1_2_q, or_8_out, bgt_p50, bgt_p51, bgt_p52, shft_1_p6, shft_1_p7, bgt_p33
  muld_div muld_div_1 ();  // open: a, b, DivQ, DivR, mulLow, mulHi
  or or_9 (or_9_out, bgt_p50, bgt_p51, bgt_p52);
  Multiplexer #(.Bits(16)) multiplexer_4 (.sel(or_9_out), .in_0({16{1'b0}}), .in_1(shft_1_p6), .out(shft_1_p7));
  byteAddrMEM byteaddrmem_1 ();  // open: dataIN, write_w, write_b, addr, Word_Not_Aligned, dataOUT, clk, read_b, read_w
  // Pins of 1 and 16 bits meet at rs4_q
  // Pins of 1 and 5 bits meet at rs4_q[4:0]

  // Notes on the sheet:
  //   IF
  //   contents of PROM (hex, n*v repeats v):
  //   ffaa,aabbccdd,0,0,0,0,0,0,0,0,0,0,0,0,0,0,0,0,0,0,0,0,0,0,0,0,0,0,0,0,0,0,0,0,0,0,
  //   0,0,0,0,0,0,0,0,0,0,0,0,0,0,0,0,0,0,0,0,0,0,0,0,0,0,0,0,0,0,0,0,0,0,0,0,0,0,0,0,0,
  //   0,0,0,0,0,0,0,0,0,0,0,0,0,0,0,0,0,0,0,0,0,0,0,0,0,0,0,0,0,0,0,0,0,0,0,0,0,0,0,0,0,
  //   0,0,0,0,0,0,0,0,0,0,0,0,0,0,0,0,0,0,0,0,0,0,0,0,0,0,0,0,0,0,0,0,0,0,0,0,0,0,0,0,0,
  //   0,0,0,0,0,0,0,0,0,0,0,0,0,0,0,0,0,0,0,0,0,0,0,0,0,0,0,0,0,0,0,0,0,0,0,0,0,0,0,0,0,
  //   0,0,0,0,0,0,0,0,0,0,0,0,0,0,0,0,0,0,0,0,0,0,0,0,0,0,0,0,0,0,0,0,aabbccdd
  //   ID
  //   jal(r)
  //   RA gets pc+1 or Rs1
  //   EX
endmodule
