// Digital circuit ID_EX.dig as structural Verilog
module ID_EX (
  input  [4:0] shft_amt,
  input  [15:0] imm,
  input  abs_rel_branch_jal_r,
  input  jmp,
  input  bgt,
  input  bgte,
  input  beq,
  input  blte,
  input  blt,
  input  bne,
  input  JALorJALR,
  input  add,
  input  sub,
  input  adc,
  input  cmp,
  input  \nor ,
  input  \and ,
  input  \xor ,
  input  \xnor ,
  input  lsl,
  input  lsr,
  input  asr,
  input  lbu,
  input  lbs,
  input  lw,
  input  sw,
  input  sb,
  input  limm,
  input  mul,
  input  muls,
  input  div,
  input  divs,
  input  branch,
  input  jal_r,
  input  clear,
  input  clk,
  output [4:0] shft_amt_2,
  output [15:0] imm_2,
  output abs_rel_branch_jal_r_2,
  output jmp_2,
  output bgt_2,
  output bgte_2,
  output beq_2,
  output blte_2,
  output blt_2,
  output bne_2,
  output JALorJJALR,
  output add_2,
  output sub_2,
  output adc_2,
  output cmp_2,
  output nor_2,
  output and_2,
  output xor_2,
  output xnor_2,
  output lsl_2,
  output lsr_2,
  output asr_2,
  output lbu_2,
  output lbs_2,
  output lw_2,
  output sw_2,
  output sb_2,
  output limm_2,
  output mul_2,
  output muls_2,
  output div_2,
  output divs_2,
  output branch_2,
  output jal_r_2
);

  D_FF_AS #(.Bits(5)) d_ff_as_1 (.Set(1'b0), .D(shft_amt), .C(clear), .Clr(clear), .Q(shft_amt_2));  // open: nQ
  D_FF_AS #(.Bits(16)) d_ff_as_2 (.Set(1'b0), .D(imm), .C(clear), .Clr(clear), .Q(imm_2));  // open: nQ
  D_FF_AS d_ff_as_3 (
    .Set(1'b0), .D(abs_rel_branch_jal_r), .C(clear), .Clr(clear), .Q(abs_rel_branch_jal_r_2));  // open: nQ
  D_FF_AS d_ff_as_4 (.Set(1'b0), .D(jmp), .C(clear), .Clr(clear), .Q(jmp_2));  // open: nQ
  D_FF_AS d_ff_as_5 (.Set(1'b0), .D(bgt), .C(clear), .Clr(clear), .Q(bgt_2));  // open: nQ
  D_FF_AS d_ff_as_6 (.Set(1'b0), .D(bgte), .C(clear), .Clr(clear), .Q(bgte_2));  // open: nQ
  D_FF_AS d_ff_as_7 (.Set(1'b0), .D(beq), .C(clear), .Clr(clear), .Q(beq_2));  // open: nQ
  D_FF_AS d_ff_as_8 (.Set(1'b0), .D(blte), .C(clear), .Clr(clear), .Q(blte_2));  // open: nQ
  D_FF_AS d_ff_as_9 (.Set(1'b0), .D(blt), .C(clear), .Clr(clear), .Q(blt_2));  // open: nQ
  D_FF_AS d_ff_as_10 (.Set(1'b0), .D(bne), .C(clear), .Clr(clear), .Q(bne_2));  // open: nQ
  D_FF_AS d_ff_as_11 (.Set(1'b0), .D(JALorJALR), .C(clear), .Clr(clear), .Q(JALorJJALR));  // open: nQ
  D_FF_AS d_ff_as_12 (.Set(1'b0), .D(add), .C(clear), .Clr(clear), .Q(add_2));  // open: nQ
  D_FF_AS d_ff_as_13 (.Set(1'b0), .D(sub), .C(clear), .Clr(clear), .Q(sub_2));  // open: nQ
  D_FF_AS d_ff_as_14 (.Set(1'b0), .D(adc), .C(clear), .Clr(clear), .Q(adc_2));  // open: nQ
  D_FF_AS d_ff_as_15 (.Set(1'b0), .D(cmp), .C(clear), .Clr(clear), .Q(cmp_2));  // open: nQ
  D_FF_AS d_ff_as_16 (.Set(1'b0), .D(\nor ), .C(clear), .Clr(clear), .Q(nor_2));  // open: nQ
  D_FF_AS d_ff_as_17 (.Set(1'b0), .D(\and ), .C(clear), .Clr(clear), .Q(and_2));  // open: nQ
  D_FF_AS d_ff_as_18 (.Set(1'b0), .D(\xor ), .C(clear), .Clr(clear), .Q(xor_2));  // open: nQ
  D_FF_AS d_ff_as_19 (.Set(1'b0), .D(\xnor ), .C(clear), .Clr(clear), .Q(xnor_2));  // open: nQ
  D_FF_AS d_ff_as_20 (.Set(1'b0), .D(lsl), .C(clear), .Clr(clear), .Q(lsl_2));  // open: nQ
  D_FF_AS d_ff_as_21 (.Set(1'b0), .D(lsr), .C(clear), .Clr(clear), .Q(lsr_2));  // open: nQ
  D_FF_AS d_ff_as_22 (.Set(1'b0), .D(asr), .C(clear), .Clr(clear), .Q(asr_2));  // open: nQ
  D_FF_AS d_ff_as_23 (.Set(1'b0), .D(lbu), .C(clear), .Clr(clear), .Q(lbu_2));  // open: nQ
  D_FF_AS d_ff_as_24 (.Set(1'b0), .D(lbs), .C(clear), .Clr(clear), .Q(lbs_2));  // open: nQ
  D_FF_AS d_ff_as_25 (.Set(1'b0), .D(lw), .C(clear), .Clr(clear), .Q(lw_2));  // open: nQ
  D_FF_AS d_ff_as_26 (.Set(1'b0), .D(sw), .C(clear), .Clr(clear), .Q(sw_2));  // open: nQ
  D_FF_AS d_ff_as_27 (.Set(1'b0), .D(sb), .C(clear), .Clr(clear), .Q(sb_2));  // open: nQ
  D_FF_AS d_ff_as_28 (.Set(1'b0), .D(limm), .C(clear), .Clr(clear), .Q(limm_2));  // open: nQ
  D_FF_AS d_ff_as_29 (.Set(1'b0), .D(mul), .C(clear), .Clr(clear), .Q(mul_2));  // open: nQ
  D_FF_AS d_ff_as_30 (.Set(1'b0), .D(muls), .C(clear), .Clr(clear), .Q(muls_2));  // open: nQ
  D_FF_AS d_ff_as_31 (.Set(1'b0), .D(div), .C(clear), .Clr(clear), .Q(div_2));  // open: nQ
  D_FF_AS d_ff_as_32 (.Set(1'b0), .D(divs), .C(clear), .Clr(clear), .Q(divs_2));  // open: nQ
  D_FF_AS d_ff_as_33 (.Set(1'b0), .D(branch), .C(clear), .Clr(clear), .Q(branch_2));  // open: nQ
  D_FF_AS d_ff_as_34 (.Set(1'b0), .D(jal_r), .C(clear), .Clr(clear), .Q(jal_r_2));  // open: nQ

  assign clk = clear;
endmodule
