// Digital circuit IF_ID.dig as structural Verilog
module IF_ID (
  input  clear,
  input  clk,
  input  [31:0] PROGRAM_IN,
  output [31:0] PROGRAM_OUT
);

  D_FF_AS #(.Bits(32)) d_ff_as_1 (.Set(1'b0), .D(PROGRAM_IN), .C(clk), .Clr(clear), .Q(PROGRAM_OUT));  // open: nQ
  // Pins of 16 and 32 bits meet at PROGRAM_OUT
endmodule
