// Digital circuit Instruction_Decoder.dig as structural Verilog
module Instruction_Decoder (
  input  [31:0] Instruction,
  output [4:0] rd,
  output [4:0] rs1,
  output [15:0] imm_16bit,
  output [4:0] shft_amt_5bit,
  output [4:0] rs2,
  output [4:0] rs3,
  output abs_rel,
  output jmp,
  output bgt,
  output bgte,
  output beq,
  output blte,
  output blt,
  output bne,
  output JALorJALR,
  output add,
  output sub,
  output adc,
  output cmp,
  output \nor ,
  output \and ,
  output \xor ,
  output \xnor ,
  output lsl,
  output lsr,
  output asr,
  output lbu,
  output lbs,
  output lw,
  output sw,
  output limm,
  output mul,
  output muls,
  output div,
  output divs,
  output branch,
  output jal_r,
  output sb
);

  wire abs_rel_BRANCH, abs_rel_JAL_R, cmp_t, not_1_out, not_2_out, not_3_out;
  wire [3:0] cond;
  wire [4:0] demultiplexer_1_out_20_2, demultiplexer_1_out_21_2, multiplexer_7_out, rd1a, rd1b, rd1c, rd1d,
       rd1e, rs1a, rs1b, rs1c, rs1d, rs1e, rs2a, rs2b, rs2c, rs2d, rs2e, rs2f;
  wire [10:0] demultiplexer_1_out_20, demultiplexer_1_out_21, or_1_out, or_3_out, or_4_out;
  wire [10:5] or_2_out;
  wire [15:0] imma, immb, immc, immd, imme, immf;
  wire [20:16] demultiplexer_1_out_15, demultiplexer_1_out_20_3;
  wire [24:22] demultiplexer_1_out_21_3;
  wire [25:0] demultiplexer_1_out_0, demultiplexer_1_out_1, demultiplexer_1_out_2, demultiplexer_1_out_3,
       demultiplexer_1_out_4, demultiplexer_1_out_5, demultiplexer_1_out_6, demultiplexer_1_out_7,
       demultiplexer_1_out_8, demultiplexer_1_out_9, demultiplexer_1_out_10, demultiplexer_1_out_11,
       demultiplexer_1_out_12, demultiplexer_1_out_13, demultiplexer_1_out_14, demultiplexer_1_out_16,
       demultiplexer_1_out_17, demultiplexer_1_out_18, demultiplexer_1_out_19, or_5_out;

  Decoder #(.Selector_Bits(6)) decoder_1 (
    .sel(Instruction[31:26]), .out_0(add), .out_1(sub), .out_2(adc), .out_3(cmp), .out_4(\nor ),
    .out_5(\and ), .out_6(\xor ), .out_7(\xnor ), .out_8(lsl), .out_9(lsr), .out_10(asr), .out_11(lbu),
    .out_12(lbs), .out_13(lw), .out_14(sw), .out_15(sb), .out_16(limm), .out_17(mul), .out_18(muls),
    .out_19(div), .out_20(divs), .out_21(branch), .out_22(jal_r));  // open: out_23, out_24, out_25, out_26, out_27, out_28, out_29, out_30, out_31, out_32, out_33, out_34, out_35, out_36, out_37, out_38, out_39, out_40, out_41, out_42, out_43, out_44, out_45, out_46, out_47, out_48, out_49, out_50, out_51, out_52, out_53, out_54, out_55, out_56, out_57, out_58, out_59, out_60, out_61, out_62, out_63
  Demultiplexer #(.Selector_Bits(6), .Bits(26)) demultiplexer_1 (
    .sel(Instruction[31:26]), .in(Instruction[25:0]), .out_0(demultiplexer_1_out_0),
    .out_1(demultiplexer_1_out_1), .out_2(demultiplexer_1_out_2), .out_3(demultiplexer_1_out_3),
    .out_4(demultiplexer_1_out_4), .out_5(demultiplexer_1_out_5), .out_6(demultiplexer_1_out_6),
    .out_7(demultiplexer_1_out_7), .out_8(demultiplexer_1_out_8), .out_9(demultiplexer_1_out_9),
    .out_10(demultiplexer_1_out_10), .out_11(demultiplexer_1_out_11), .out_12(demultiplexer_1_out_12),
    .out_13(demultiplexer_1_out_13), .out_14(demultiplexer_1_out_14),
    .out_15({rd1d, demultiplexer_1_out_15, immd}), .out_16(demultiplexer_1_out_16),
    .out_17(demultiplexer_1_out_17), .out_18(demultiplexer_1_out_18), .out_19(demultiplexer_1_out_19),
    .out_20({cond, abs_rel_BRANCH, demultiplexer_1_out_20_3, demultiplexer_1_out_20_2, demultiplexer_1_out_20}),
    .out_21({JALorJALR, demultiplexer_1_out_21_3, abs_rel_JAL_R, rd1e, demultiplexer_1_out_21_2, demultiplexer_1_out_21}));  // open: out_22, out_23, out_24, out_25, out_26, out_27, out_28, out_29, out_30, out_31, out_32, out_33, out_34, out_35, out_36, out_37, out_38, out_39, out_40, out_41, out_42, out_43, out_44, out_45, out_46, out_47, out_48, out_49, out_50, out_51, out_52, out_53, out_54, out_55, out_56, out_57, out_58, out_59, out_60, out_61, out_62, out_63
  assign {rd1a, rs1a, rs2a, or_1_out} = demultiplexer_1_out_0 | demultiplexer_1_out_1 | demultiplexer_1_out_2 | demultiplexer_1_out_3 | demultiplexer_1_out_4 | demultiplexer_1_out_5 | demultiplexer_1_out_6;  // Or or_1, 26 bits wide
  assign {rd1b, rs2b, rs1b, or_2_out, shft_amt_5bit} = demultiplexer_1_out_7 | demultiplexer_1_out_8 | demultiplexer_1_out_9;  // Or or_2, 26 bits wide
  assign {rd1c, rs1c, rs2c, or_3_out} = demultiplexer_1_out_10 | demultiplexer_1_out_11 | demultiplexer_1_out_12;  // Or or_3, 26 bits wide
  assign {rs3, rs1d, rs2d, or_4_out} = demultiplexer_1_out_13 | demultiplexer_1_out_14;  // Or or_4, 26 bits wide
  assign {or_5_out[25:21], rs1e, or_5_out[15:0]} = demultiplexer_1_out_16 | demultiplexer_1_out_17 | demultiplexer_1_out_18 | demultiplexer_1_out_19;  // Or or_5, 26 bits wide
  BitExtender bitextender_1 (.in(or_1_out[7:0]), .out(imma));
  BitExtender #(.inputBits(11)) bitextender_2 (.in(or_3_out), .out(immb));
  BitExtender #(.inputBits(11)) bitextender_3 (.in(or_4_out), .out(immc));
  not not_1 (not_1_out, demultiplexer_1_out_20_3[20]);
  Multiplexer #(.Bits(16)) multiplexer_1 (
    .sel(not_1_out), .in_0({16{1'b0}}), .in_1({demultiplexer_1_out_20, demultiplexer_1_out_20_2}), .out(immf));
  Multiplexer #(.Bits(5)) multiplexer_2 (
    .sel(demultiplexer_1_out_20_3[20]), .in_0({5{1'b0}}), .in_1(demultiplexer_1_out_20_2), .out(rs2f));
  not not_2 (not_2_out, demultiplexer_1_out_21_3[22]);
  Multiplexer #(.Bits(16)) multiplexer_3 (
    .sel(not_2_out), .in_0({16{1'b0}}), .in_1({demultiplexer_1_out_21, demultiplexer_1_out_21_2}), .out(immf));
  Multiplexer #(.Bits(5)) multiplexer_4 (
    .sel(demultiplexer_1_out_21_3[22]), .in_0({5{1'b0}}), .in_1(demultiplexer_1_out_21_2), .out(rs2f));
  not not_3 (not_3_out, or_5_out[21]);
  Multiplexer #(.Bits(16)) multiplexer_5 (
    .sel(not_3_out), .in_0({16{1'b0}}), .in_1({or_5_out[10:0], or_5_out[15:11]}), .out(imme));
  Multiplexer #(.Bits(5)) multiplexer_6 (.sel(or_5_out[21]), .in_0({5{1'b0}}), .in_1(or_5_out[15:11]), .out(rs2e));
  Multiplexer #(.Bits(5)) multiplexer_7 (.sel(cmp_t), .in_0(rd1a), .in_1({5{1'b0}}), .out(multiplexer_7_out));
  assign rd = rd1d | rd1b | rd1e | rd1c | multiplexer_7_out;  // Or or_6, 5 bits wide
  assign rs1 = rs1b | rs1c | rs1a | rs1d | rs1e;  // Or or_7, 5 bits wide
  assign rs2 = rs2a | rs2b | rs2e | rs2d | rs2c | rs2f;  // Or or_8, 5 bits wide
  assign imm_16bit = imma | immb | imme | immd | immc | immf;  // Or or_9, 16 bits wide
  or or_10 (abs_rel, abs_rel_BRANCH, abs_rel_JAL_R);
  Decoder #(.Selector_Bits(4)) decoder_2 (
    .sel(cond), .out_0(jmp), .out_1(bgt), .out_2(bgte), .out_3(beq), .out_4(blte), .out_5(blt), .out_6(bne));  // open: out_7, out_8, out_9, out_10, out_11, out_12, out_13, out_14, out_15

  // Other names for the same wires on the sheet: shftAMT[4:0] = shft_amt_5bit

  // Notes on the sheet:
  //   ALU OPs
  //   update ALU flags
  //   on CMP update CMP flags
  //   Shft
  //   Load/Store
  //   shft Ops(3)
  //   Load Ops(3)
  //   STORE(2)
  //   mul/div
  //   branch and jmp
  //   ALU Ops(7)
  //   MUL/DIV(4)
  //   BRANCH(1)
  //   JAL(R)(1)
  //   LIMM(1)
  //   COND			
  //   0	jmp			
  //   1	bgt 			
  //   2	bgte			
  //   3	beq			
  //   4	blte			
  //   5	blt			
  //   6	bne
endmodule
