// Digital circuit ProgramCounter.dig as structural Verilog
module ProgramCounter (
  input  abs_rel,
  input  [15:0] branch_input,
  input  branchEnable,
  input  clk,
  output [15:0] PROMaddr
);

  wire [15:0] add_1_s, multiplexer_1_out;

  Add #(.Bits(16)) add_1 (.a(branch_input), .b(multiplexer_1_out), .c_i(1'b0), .s(add_1_s));  // open: c_o
  CounterPreset #(.Bits(16)) counterpreset_1 (
    .en(1'b1), .C(clk), .dir(1'b0), .in(add_1_s), .ld(branchEnable), .clr(1'b0), .out(PROMaddr));  // open: ovf
  Multiplexer #(.Bits(16)) multiplexer_1 (.sel(abs_rel), .in_0({16{1'b0}}), .in_1(PROMaddr), .out(multiplexer_1_out));
endmodule
