// Digital circuit byteAddrMEM.dig as structural Verilog
module byteAddrMEM (
  input  [15:0] dataIN,
  input  write_w,
  input  write_b,
  input  [15:0] addr,
  input  clk,
  input  read_b,
  input  read_w,
  output Word_Not_Aligned,
  output [15:0] dataOUT
);

  wire and_1_out, and_2_out, and_3_out, and_4_out, and_5_out, and_6_out, and_7_out, and_8_out, and_9_out,
       and_10_out, multiplexer_1_out, multiplexer_7_out, not_1_out, or_1_out, or_2_out, or_5_out, or_6_out,
       or_7_out;
  wire [7:0] demultiplexer_1_out_0, demultiplexer_1_out_1, multiplexer_3_out, multiplexer_4_out,
       multiplexer_5_out, multiplexer_6_out, multiplexer_8_out, multiplexer_9_out, or_3_out, or_8_out,
       ramdualport_1_d, ramdualport_2_d;

  and and_1 (and_1_out, write_w, ~addr[0]);  // And
  and and_2 (and_2_out, ~addr[0], read_w);  // And
  or or_1 (or_1_out, read_w, and_3_out);
  and and_3 (and_3_out, addr[0], read_b);
  and and_4 (and_4_out, write_b, addr[0]);
  or or_2 (or_2_out, and_4_out, and_1_out);
  Multiplexer multiplexer_1 (.sel(and_8_out), .in_0(or_2_out), .in_1(1'b0), .out(multiplexer_1_out));
  Multiplexer #(.Bits(8)) multiplexer_2 (
    .sel(and_2_out), .in_0({8{1'b0}}), .in_1(ramdualport_1_d), .out(dataOUT[15:8]));
  Multiplexer #(.Bits(8)) multiplexer_3 (
    .sel(not_1_out), .in_0({8{1'b0}}), .in_1(dataIN[15:8]), .out(multiplexer_3_out));
  assign or_3_out = multiplexer_5_out | multiplexer_3_out;  // Or or_3, 8 bits wide
  RAMDualPort #(.AddrBits(15), .Bits(8)) ramdualport_1 (
    .A(addr[15:1]), .Din(or_3_out), .str(multiplexer_1_out), .C(clk), .ld(or_1_out), .D(ramdualport_1_d));
  Multiplexer #(.Bits(8)) multiplexer_4 (
    .sel(and_5_out), .in_0({8{1'b0}}), .in_1(ramdualport_1_d), .out(multiplexer_4_out));
  Multiplexer #(.Bits(8)) multiplexer_5 (
    .sel(write_b), .in_0({8{1'b0}}), .in_1(demultiplexer_1_out_1), .out(multiplexer_5_out));
  and and_5 (and_5_out, read_b, addr[0]);
  Demultiplexer #(.Bits(8)) demultiplexer_1 (
    .sel(addr[0]), .in(dataIN[7:0]), .out_0(demultiplexer_1_out_0), .out_1(demultiplexer_1_out_1));
  not not_1 (not_1_out, write_b);
  assign dataOUT[7:0] = multiplexer_8_out | multiplexer_4_out;  // Or or_4, 8 bits wide
  and and_6 (and_6_out, ~addr[0], read_b);  // And
  and and_7 (and_7_out, ~addr[0], read_b);  // And
  or or_5 (or_5_out, and_6_out, read_w);
  or or_6 (or_6_out, and_7_out, and_2_out);
  and and_8 (and_8_out, write_w, addr[0]);
  and and_9 (and_9_out, write_b, ~addr[0]);  // And
  or or_7 (or_7_out, and_1_out, and_9_out);
  Multiplexer #(.Bits(8)) multiplexer_6 (
    .sel(not_1_out), .in_0({8{1'b0}}), .in_1(dataIN[7:0]), .out(multiplexer_6_out));
  assign or_8_out = multiplexer_9_out | multiplexer_6_out;  // Or or_8, 8 bits wide
  Multiplexer multiplexer_7 (.sel(and_8_out), .in_0(or_7_out), .in_1(1'b0), .out(multiplexer_7_out));
  RAMDualPort #(.AddrBits(15), .Bits(8)) ramdualport_2 (
    .A(addr[15:1]), .Din(or_8_out), .str(multiplexer_7_out), .C(clk), .ld(or_5_out), .D(ramdualport_2_d));
  Multiplexer #(.Bits(8)) multiplexer_8 (
    .sel(or_6_out), .in_0({8{1'b0}}), .in_1(ramdualport_2_d), .out(multiplexer_8_out));
  and and_10 (and_10_out, addr[0], read_w);
  Multiplexer #(.Bits(8)) multiplexer_9 (
    .sel(write_b), .in_0({8{1'b0}}), .in_1(demultiplexer_1_out_0), .out(multiplexer_9_out));
  or or_9 (Word_Not_Aligned, and_8_out, and_10_out);
endmodule
