// Digital circuit failedbyteaddressRAM.dig as structural Verilog
module failedbyteaddressRAM (
  input  [15:0] data,
  input  write_w,
  input  write_b,
  input  [15:0] addr,
  input  clk,
  output Word_Not_Aligned,
  output [15:0] out_6
);

  wire and_1_out, and_2_out, and_4_out, or_1_out, or_2_out;

  and and_1 (and_1_out, write_w, addr[0]);
  and and_2 (and_2_out, write_b, addr[0]);
  or or_1 (or_1_out, and_2_out, and_1_out);
  BlockRAMDualPort #(.AddrBits(15), .Bits(8)) blockramdualport_1 (
    .A(addr[15:1]), .Din(data[15:8]), .str(or_1_out), .C(clk), .D(out_6[15:8]));
  and and_3 (Word_Not_Aligned, write_w, ~addr[0]);  // And
  and and_4 (and_4_out, write_b, ~addr[0]);  // And
  or or_2 (or_2_out, and_1_out, and_4_out);
  BlockRAMDualPort #(.AddrBits(15), .Bits(8)) blockramdualport_2 (
    .A(addr[15:1]), .Din(data[7:0]), .str(or_2_out), .C(clk), .D(out_6[7:0]));
endmodule
