// Digital circuit muld_div.dig as structural Verilog
module muld_div (
  input  [15:0] a,
  input  [15:0] b,
  output [15:0] DivQ,
  output [15:0] DivR,
  output [15:0] mulLow,
  output [15:0] mulHi
);

  Mul #(.Bits(16)) mul_1 (.a(a), .b(b), .mul({mulHi, mulLow}));
  Div #(.Bits(16)) div_1 (.a(a), .b(b), .q(DivQ), .r(DivR));
endmodule
