// Digital circuit riiscv1.dig as structural Verilog
module riiscv1 (
  input  [15:0] a,
  input  [15:0] b,
  input  updatealuflag,
  input  updatecmpflag,
  input  cin,
  input  \xnor ,
  input  \xor ,
  input  \nor ,
  input  \and ,
  input  sub,
  input  add,
  input  adc,
  output blt,
  output beq,
  output bgt,
  output [15:0] out,
  output coutreg,
  output if0reg,
  output n_a
);

  wire add_1_c_o, comparator_1_eq, comparator_1_gt, comparator_1_lt, multiplexer_1_out, or_1_out, or_2_out;
  wire [15:0] add_1_s, and_1_out, multiplexer_2_out, multiplexer_3_out, multiplexer_4_out, multiplexer_5_out,
       multiplexer_6_out, multiplexer_7_out, nor_1_out, sub_1_s, xnor_1_out, xor_1_out;

  or or_1 (or_1_out, cin, multiplexer_1_out);
  Multiplexer multiplexer_1 (.sel(adc), .in_0(1'b0), .in_1(coutreg), .out(multiplexer_1_out));
  Add #(.Bits(16)) add_1 (.a(a), .b(b), .c_i(or_1_out), .s(add_1_s), .c_o(add_1_c_o));
  Sub #(.Bits(16)) sub_1 (.a(a), .b(b), .c_i(1'b0), .s(sub_1_s), .c_o(n_a));
  Comparator #(.Bits(16)) comparator_1 (.a(a), .b(b), .gt(comparator_1_gt), .eq(comparator_1_eq), .lt(comparator_1_lt));
  assign and_1_out = a & b;  // And and_1, 16 bits wide
  assign nor_1_out = ~(a | b);  // NOr nor_1, 16 bits wide
  assign xor_1_out = a ^ b;  // XOr xor_1, 16 bits wide
  assign xnor_1_out = ~(a ^ b);  // XNOr xnor_1, 16 bits wide
  D_FF gt (.D(comparator_1_gt), .C(updatecmpflag), .Q(bgt));  // open: nQ
  D_FF eq (.D(comparator_1_eq), .C(updatecmpflag), .Q(beq));  // open: nQ
  D_FF lt (.D(comparator_1_lt), .C(updatecmpflag), .Q(blt));  // open: nQ
  Multiplexer #(.Bits(16)) multiplexer_2 (.sel(\xnor ), .in_0({16{1'b0}}), .in_1(xnor_1_out), .out(multiplexer_2_out));
  Multiplexer #(.Bits(16)) multiplexer_3 (.sel(\nor ), .in_0({16{1'b0}}), .in_1(nor_1_out), .out(multiplexer_3_out));
  Multiplexer #(.Bits(16)) multiplexer_4 (.sel(\xor ), .in_0({16{1'b0}}), .in_1(xor_1_out), .out(multiplexer_4_out));
  Multiplexer #(.Bits(16)) multiplexer_5 (.sel(sub), .in_0({16{1'b0}}), .in_1(sub_1_s), .out(multiplexer_5_out));
  Multiplexer #(.Bits(16)) multiplexer_6 (.sel(\and ), .in_0({16{1'b0}}), .in_1(and_1_out), .out(multiplexer_6_out));
  Multiplexer #(.Bits(16)) multiplexer_7 (.sel(add), .in_0({16{1'b0}}), .in_1(add_1_s), .out(multiplexer_7_out));
  or or_2 (or_2_out, add_1_s[0], add_1_s[1], add_1_s[2], add_1_s[3], add_1_s[4], add_1_s[5], add_1_s[6], add_1_s[7], add_1_s[8], add_1_s[9], add_1_s[10], add_1_s[11], add_1_s[12], add_1_s[13], add_1_s[14], add_1_s[15]);
  assign out = multiplexer_7_out | multiplexer_5_out | multiplexer_6_out | multiplexer_3_out | multiplexer_4_out | multiplexer_2_out;  // Or or_3, 16 bits wide
  D_FF cout (.D(add_1_c_o), .C(updatealuflag), .Q(coutreg));  // open: nQ
  D_FF if0 (.D(or_2_out), .C(updatealuflag), .Q(if0reg));  // open: nQ
endmodule
