// Digital circuit shft.dig as structural Verilog
module shft (
  input  [15:0] Din,
  input  [15:0] shft_amt,
  input  lsl,
  input  lsr,
  input  asr,
  output [15:0] dout
);

  wire [15:0] barrelshifter_1_out, barrelshifter_2_out, barrelshifter_3_out, multiplexer_1_out,
       multiplexer_2_out, multiplexer_3_out;

  BarrelShifter #(.Bits(16)) barrelshifter_1 (.in(Din), .shift(shft_amt[4:0]), .out(barrelshifter_1_out));
  BarrelShifter #(.Bits(16), .direction("right")) barrelshifter_2 (
    .in(Din), .shift(shft_amt[4:0]), .out(barrelshifter_2_out));
  BarrelShifter #(.Bits(16), .barrelShifterMode("arithmetic"), .direction("right")) barrelshifter_3 (
    .in(Din), .shift(shft_amt[4:0]), .out(barrelshifter_3_out));
  Multiplexer #(.Bits(16)) multiplexer_1 (
    .sel(lsl), .in_0({16{1'b0}}), .in_1(barrelshifter_1_out), .out(multiplexer_1_out));
  Multiplexer #(.Bits(16)) multiplexer_2 (
    .sel(lsr), .in_0({16{1'b0}}), .in_1(barrelshifter_2_out), .out(multiplexer_2_out));
  assign dout = multiplexer_1_out | multiplexer_2_out | multiplexer_3_out;  // Or or_1, 16 bits wide
  Multiplexer #(.Bits(16)) multiplexer_3 (
    .sel(asr), .in_0({16{1'b0}}), .in_1(barrelshifter_3_out), .out(multiplexer_3_out));

  // Notes on the sheet:
  //   SHIFT			
  //   		XLEN1 = 5bitUnsignedInt			
  //   rd[] <= rs1 << rs2	4	lsl rd, rs1, rs2	lsl rd, rs1, imm(XLEN1)	4	rd[] <= rs1[] << imm
  //   rd[] <= rs1 >> rs2	4	lsr rd, rs1, rs2	lsr rd, rs1, imm(XLEN1)	4	rd[] <= rs1[] >> imm
  //   rd[] <= rs1 >>> rs2	4	asr rd, rs1, rs2	asr rd, rs1, imm(XLEN1)	4	rd[] <= rs1[] >>> imm
endmodule
