// Digital circuit CPU.dig as structural Verilog
module CPU (
);

  wire triportregs_1_p1, triportregs_1_p2;

  // TriPortRegs triportregs_1: pin names not known; wires that end beside it: triportregs_1_p1, triportregs_1_p2
  // riiscv1 riiscv1_1: pin names not known; wires that end beside it: triportregs_1_p1, triportregs_1_p2
  // shft shft_1: pin names not known; wires that end beside it: triportregs_1_p1, triportregs_1_p2
  // muld_div muld_div_1: pin names not known; wires that end beside it: triportregs_1_p1, triportregs_1_p2
endmodule
