// Digital circuit Instruction_Decoder.dig as structural Verilog
module Instruction_Decoder (
  input  [31:0] Instruction,
  output [4:0] rd,
  output [4:0] rs1,
  output [15:0] imm_16bit,
  output [4:0] shft_amt_5bit,
  output [4:0] rs3,
  output mul_div_imm_or_rs2,
  output [4:0] rs2
);

  wire adc, add, \and , asr, cmp, div, divs, lbs, lbu, limm, lsl, lsr, lw, mul, muls, \nor , sub, sw, \xnor ,
       \xor ;
  wire [4:0] demultiplexer_1_out_13_2, demultiplexer_1_out_14_2, multiplexer_1_out, or_3_out_2, or_3_out_3,
       or_4_out_2, rs2a, rs2b, rs2c, rs2d, rs2e;
  wire [10:0] demultiplexer_1_out_13, or_3_out;
  wire [15:0] imma, immb, immc, immd;
  wire [20:16] demultiplexer_1_out_14;
  wire [25:0] demultiplexer_1_out_0, demultiplexer_1_out_1, demultiplexer_1_out_2, demultiplexer_1_out_3,
       demultiplexer_1_out_4, demultiplexer_1_out_5, demultiplexer_1_out_6, demultiplexer_1_out_7,
       demultiplexer_1_out_8, demultiplexer_1_out_9, demultiplexer_1_out_10, demultiplexer_1_out_11,
       demultiplexer_1_out_12, demultiplexer_1_out_15, demultiplexer_1_out_16, demultiplexer_1_out_17,
       demultiplexer_1_out_18, demultiplexer_1_out_19, demultiplexer_1_out_20, or_1_out, or_4_out;
  wire [25:5] or_2_out;

  Demultiplexer #(.Bits(26), .Selector_Bits(6)) demultiplexer_1 (
    .sel(Instruction[31:26]), .in(Instruction[25:0]), .out_0(demultiplexer_1_out_0),
    .out_1(demultiplexer_1_out_1), .out_2(demultiplexer_1_out_2), .out_3(demultiplexer_1_out_3),
    .out_4(demultiplexer_1_out_4), .out_5(demultiplexer_1_out_5), .out_6(demultiplexer_1_out_6),
    .out_7(demultiplexer_1_out_7), .out_8(demultiplexer_1_out_8), .out_9(demultiplexer_1_out_9),
    .out_10(demultiplexer_1_out_10), .out_11(demultiplexer_1_out_11), .out_12(demultiplexer_1_out_12),
    .out_13({rs3, demultiplexer_1_out_13_2, rs2d, demultiplexer_1_out_13}),
    .out_14({demultiplexer_1_out_14_2, demultiplexer_1_out_14, immd}), .out_15(demultiplexer_1_out_15),
    .out_16(demultiplexer_1_out_16), .out_17(demultiplexer_1_out_17), .out_18(demultiplexer_1_out_18),
    .out_19(demultiplexer_1_out_19), .out_20(demultiplexer_1_out_20));  // open: out_21, out_22, out_23, out_24, out_25, out_26, out_27, out_28, out_29, out_30, out_31, out_32, out_33, out_34, out_35, out_36, out_37, out_38, out_39, out_40, out_41, out_42, out_43, out_44, out_45, out_46, out_47, out_48, out_49, out_50, out_51, out_52, out_53, out_54, out_55, out_56, out_57, out_58, out_59, out_60, out_61, out_62, out_63
  assign {or_1_out[25:16], rs2a, or_1_out[10:0]} = demultiplexer_1_out_0 | demultiplexer_1_out_1 | demultiplexer_1_out_2 | demultiplexer_1_out_3 | demultiplexer_1_out_4 | demultiplexer_1_out_5 | demultiplexer_1_out_6;  // Or or_1, 26 bits wide
  assign {or_2_out[25:16], rs2b, or_2_out[10:5], shft_amt_5bit} = demultiplexer_1_out_7 | demultiplexer_1_out_8 | demultiplexer_1_out_9;  // Or or_2, 26 bits wide
  assign {or_3_out_3, or_3_out_2, rs2c, or_3_out} = demultiplexer_1_out_10 | demultiplexer_1_out_11 | demultiplexer_1_out_12;  // Or or_3, 26 bits wide
  assign {or_4_out[25:22], mul_div_imm_or_rs2, or_4_out_2, rs2e, or_4_out[10:0]} = demultiplexer_1_out_15 | demultiplexer_1_out_16 | demultiplexer_1_out_17 | demultiplexer_1_out_18;  // Or or_4, 26 bits wide
  Decoder #(.Selector_Bits(6)) decoder_1 (
    .sel(Instruction[31:26]), .out_0(add), .out_1(sub), .out_2(adc), .out_3(cmp), .out_4(\nor ),
    .out_5(\and ), .out_6(\xor ), .out_7(\xnor ), .out_8(lsl), .out_9(lsr), .out_10(asr), .out_11(lbu),
    .out_12(lbs), .out_13(lw), .out_14(sw), .out_15(limm), .out_16(mul), .out_17(muls), .out_18(div),
    .out_19(divs));  // open: out_20, out_21, out_22, out_23, out_24, out_25, out_26, out_27, out_28, out_29, out_30, out_31, out_32, out_33, out_34, out_35, out_36, out_37, out_38, out_39, out_40, out_41, out_42, out_43, out_44, out_45, out_46, out_47, out_48, out_49, out_50, out_51, out_52, out_53, out_54, out_55, out_56, out_57, out_58, out_59, out_60, out_61, out_62, out_63
  BitExtender #(.inputBits(11)) bitextender_1 (.in(demultiplexer_1_out_13), .out(immc));
  BitExtender #(.inputBits(11)) bitextender_2 (.in(or_3_out), .out(immb));
  BitExtender bitextender_3 (.in(or_1_out[7:0]), .out(imma));
  Multiplexer #(.Bits(5)) multiplexer_1 (.sel(cmp), .in_0({5{1'b0}}), .in_1(or_1_out[25:21]), .out(multiplexer_1_out));
  assign rd = demultiplexer_1_out_14_2 | or_2_out[25:21] | or_3_out_3 | multiplexer_1_out;  // Or or_5, 5 bits wide
  assign rs1 = or_2_out[20:16] | or_3_out_2 | or_1_out[20:16] | demultiplexer_1_out_13_2 | or_4_out_2;  // Or or_6, 5 bits wide
  assign imm_16bit = imma | immb | immc | immd;  // Or or_7, 16 bits wide
  assign rs2 = rs2a | rs2b | rs2e | rs2c | rs2d;  // Or or_8, 5 bits wide

  // Notes on the sheet:
  //   ALU Ops(7)
  //   shft Ops(3)
  //   Load Ops(3)
  //   LIMM(1)
  //   JAL(R)(1)
  //   STORE(1)
  //   MUL/DIV(4)
  //   BRANCH(1)
  //   ALU OPs
  //   update ALU flags
  //   on CMP update CMP flags
  //   Shft
  //   Load/Store
  //   mul/div
endmodule
