// Digital circuit dualportRegs.dig as structural Verilog
module dualportRegs (
  input  [15:0] saved_temp_index_and_pointer,
  input  [15:0] mhdata,
  input  [15:0] mldata,
  input  [15:0] dqdata,
  input  [15:0] drdata,
  input  [4:0] src1addr,
  input  [4:0] src2addr,
  input  [4:0] src3addr,
  input  [4:0] waddr,
  input  muldivclock,
  input  s_t_i_p_clock,
  output [15:0] src1,
  output [15:0] src2,
  output [15:0] src3
);

  wire decoder_4_out_1, decoder_4_out_2, decoder_4_out_3, decoder_4_out_4, decoder_4_out_5, decoder_4_out_6,
       decoder_4_out_7, decoder_4_out_8, decoder_4_out_9, decoder_4_out_10, decoder_4_out_11,
       decoder_4_out_12, decoder_4_out_13, decoder_4_out_14, decoder_4_out_15, decoder_4_out_16,
       decoder_4_out_17, decoder_4_out_18, decoder_4_out_19, decoder_4_out_20, decoder_4_out_21,
       decoder_4_out_22, decoder_4_out_23, decoder_4_out_28, decoder_4_out_29, decoder_4_out_30,
       decoder_4_out_31, src1r1, src1r2, src1r3, src1r4, src1r5, src1r6, src1r7, src1r8, src1r9, src1r10,
       src1r11, src1r12, src1r13, src1r14, src1r15, src1r16, src1r17, src1r18, src1r19, src1r20, src1r21,
       src1r22, src1r23, src1r24, src1r25, src1r26, src1r27, src1r28, src1r29, src1r30, src1r31, src2r1,
       src2r2, src2r3, src2r4, src2r5, src2r6, src2r7, src2r8, src2r9, src2r10, src2r11, src2r12, src2r13,
       src2r14, src2r15, src2r16, src2r17, src2r18, src2r19, src2r20, src2r21, src2r22, src2r23, src2r24,
       src2r25, src2r26, src2r27, src2r28, src2r29, src2r30, src2r31, src3r1, src3r2, src3r3, src3r4, src3r5,
       src3r6, src3r7, src3r8, src3r9, src3r10, src3r11, src3r12, src3r13, src3r14, src3r15, src3r16,
       src3r17, src3r18, src3r19, src3r20, src3r21, src3r22, src3r23, src3r24, src3r25, src3r26, src3r27,
       src3r28, src3r29, src3r30, src3r31;
  wire [15:0] dq_q, dr_q, fp_q, gp_q, ix_q, iy_q, mh_q, ml_q, ra_q, s0_q, s1_q, s2_q, s3_q, s4_q, s5_q, s6_q,
       s7_q, s8_q, sp_q, src1b1, src1b2, src1b3, src1b4, src1b5, src1b6, src1b7, src1b8, src1b9, src1b10,
       src1b11, src1b12, src1b13, src1b14, src1b15, src1b16, src1b17, src1b18, src1b19, src1b20, src1b21,
       src1b22, src1b23, src1b24, src1b25, src1b26, src1b27, src1b28, src1b29, src1b30, src1b31, src2b1,
       src2b2, src2b3, src2b4, src2b5, src2b6, src2b7, src2b8, src2b9, src2b10, src2b11, src2b12, src2b13,
       src2b14, src2b15, src2b16, src2b17, src2b18, src2b19, src2b20, src2b21, src2b22, src2b23, src2b24,
       src2b25, src2b26, src2b27, src2b28, src2b29, src2b30, src2b31, src3b1, src3b2, src3b3, src3b4, src3b5,
       src3b6, src3b7, src3b8, src3b9, src3b10, src3b11, src3b12, src3b13, src3b14, src3b15, src3b16,
       src3b17, src3b18, src3b19, src3b20, src3b21, src3b22, src3b23, src3b24, src3b25, src3b26, src3b27,
       src3b28, src3b29, src3b30, src3b31, t0_q, t1_q, t2_q, t3_q, t4_q, t5_q, t6_q, t7_q, t8_q, t9_q, t10_q,
       t11_q;

  Decoder #(.Selector_Bits(5)) decoder_1 (
    .sel(src1addr), .out_1(src1r1), .out_2(src1r2), .out_3(src1r3), .out_4(src1r4), .out_5(src1r5),
    .out_6(src1r6), .out_7(src1r7), .out_8(src1r8), .out_9(src1r9), .out_10(src1r10), .out_11(src1r11),
    .out_12(src1r12), .out_13(src1r13), .out_14(src1r14), .out_15(src1r15), .out_16(src1r16),
    .out_17(src1r17), .out_18(src1r18), .out_19(src1r19), .out_20(src1r20), .out_21(src1r21),
    .out_22(src1r22), .out_23(src1r23), .out_24(src1r24), .out_25(src1r25), .out_26(src1r26),
    .out_27(src1r27), .out_28(src1r28), .out_29(src1r29), .out_30(src1r30), .out_31(src1r31));  // open: out_0
  Decoder #(.Selector_Bits(5)) decoder_2 (
    .sel(src2addr), .out_1(src2r1), .out_2(src2r2), .out_3(src2r3), .out_4(src2r4), .out_5(src2r5),
    .out_6(src2r6), .out_7(src2r7), .out_8(src2r8), .out_9(src2r9), .out_10(src2r10), .out_11(src2r11),
    .out_12(src2r12), .out_13(src2r13), .out_14(src2r14), .out_15(src2r15), .out_16(src2r16),
    .out_17(src2r17), .out_18(src2r18), .out_19(src2r19), .out_20(src2r20), .out_21(src2r21),
    .out_22(src2r22), .out_23(src2r23), .out_24(src2r24), .out_25(src2r25), .out_26(src2r26),
    .out_27(src2r27), .out_28(src2r28), .out_29(src2r29), .out_30(src2r30), .out_31(src2r31));  // open: out_0
  Decoder #(.Selector_Bits(5)) decoder_3 (
    .sel(src3addr), .out_1(src3r1), .out_2(src3r2), .out_3(src3r3), .out_4(src3r4), .out_5(src3r5),
    .out_6(src3r6), .out_7(src3r7), .out_8(src3r8), .out_9(src3r9), .out_10(src3r10), .out_11(src3r11),
    .out_12(src3r12), .out_13(src3r13), .out_14(src3r14), .out_15(src3r15), .out_16(src3r16),
    .out_17(src3r17), .out_18(src3r18), .out_19(src3r19), .out_20(src3r20), .out_21(src3r21),
    .out_22(src3r22), .out_23(src3r23), .out_24(src3r24), .out_25(src3r25), .out_26(src3r26),
    .out_27(src3r27), .out_28(src3r28), .out_29(src3r29), .out_30(src3r30), .out_31(src3r31));  // open: out_0
  assign src1 = src1b31 | src1b30 | src1b29 | src1b28 | src1b27 | src1b26 | src1b25 | src1b24 | src1b23 | src1b22 | src1b21 | src1b20 | src1b19 | src1b18 | src1b17 | src1b16 | src1b15 | src1b14 | src1b13 | src1b12 | src1b11 | src1b10 | src1b9 | src1b8 | src1b7 | src1b6 | src1b5 | src1b4 | src1b3 | src1b2 | src1b1;  // Or or_1, 16 bits wide
  assign src2 = src2b31 | src2b30 | src2b29 | src2b28 | src2b27 | src2b26 | src2b25 | src2b24 | src2b23 | src2b22 | src2b21 | src2b20 | src2b19 | src2b18 | src2b17 | src2b16 | src2b15 | src2b14 | src2b13 | src2b12 | src2b11 | src2b10 | src2b9 | src2b8 | src2b7 | src2b6 | src2b5 | src2b4 | src2b3 | src2b2 | src2b1;  // Or or_2, 16 bits wide
  assign src3 = src3b31 | src3b30 | src3b29 | src3b28 | src3b27 | src3b26 | src3b25 | src3b24 | src3b23 | src3b22 | src3b21 | src3b20 | src3b19 | src3b18 | src3b17 | src3b16 | src3b15 | src3b14 | src3b13 | src3b12 | src3b11 | src3b10 | src3b9 | src3b8 | src3b7 | src3b6 | src3b5 | src3b4 | src3b3 | src3b2 | src3b1;  // Or or_3, 16 bits wide
  Multiplexer #(.Bits(16)) multiplexer_1 (.sel(src1r1), .in_0({16{1'b0}}), .in_1(t0_q), .out(src1b1));
  Register #(.Bits(16)) t0 (.D(saved_temp_index_and_pointer), .C(s_t_i_p_clock), .en(decoder_4_out_1), .Q(t0_q));
  Multiplexer #(.Bits(16)) multiplexer_2 (.sel(src2r1), .in_0({16{1'b0}}), .in_1(t0_q), .out(src2b1));
  Multiplexer #(.Bits(16)) multiplexer_3 (.sel(src3r1), .in_0({16{1'b0}}), .in_1(t0_q), .out(src3b1));
  Multiplexer #(.Bits(16)) multiplexer_4 (.sel(src1r2), .in_0({16{1'b0}}), .in_1(t1_q), .out(src1b2));
  Multiplexer #(.Bits(16)) multiplexer_5 (.sel(src2r2), .in_0({16{1'b0}}), .in_1(t1_q), .out(src2b2));
  Register #(.Bits(16)) t1 (.D(saved_temp_index_and_pointer), .C(s_t_i_p_clock), .en(decoder_4_out_2), .Q(t1_q));
  Multiplexer #(.Bits(16)) multiplexer_6 (.sel(src1r3), .in_0({16{1'b0}}), .in_1(t2_q), .out(src1b3));
  Multiplexer #(.Bits(16)) multiplexer_7 (.sel(src3r2), .in_0({16{1'b0}}), .in_1(t1_q), .out(src3b2));
  Register #(.Bits(16)) t2 (.D(saved_temp_index_and_pointer), .C(s_t_i_p_clock), .en(decoder_4_out_3), .Q(t2_q));
  Multiplexer #(.Bits(16)) multiplexer_8 (.sel(src2r3), .in_0({16{1'b0}}), .in_1(t2_q), .out(src2b3));
  Multiplexer #(.Bits(16)) multiplexer_9 (.sel(src3r3), .in_0({16{1'b0}}), .in_1(t2_q), .out(src3b3));
  Multiplexer #(.Bits(16)) multiplexer_10 (.sel(src1r4), .in_0({16{1'b0}}), .in_1(t3_q), .out(src1b4));
  Multiplexer #(.Bits(16)) multiplexer_11 (.sel(src2r4), .in_0({16{1'b0}}), .in_1(t3_q), .out(src2b4));
  Register #(.Bits(16)) t3 (.D(saved_temp_index_and_pointer), .C(s_t_i_p_clock), .en(decoder_4_out_4), .Q(t3_q));
  Multiplexer #(.Bits(16)) multiplexer_12 (.sel(src1r5), .in_0({16{1'b0}}), .in_1(t4_q), .out(src1b5));
  Multiplexer #(.Bits(16)) multiplexer_13 (.sel(src3r4), .in_0({16{1'b0}}), .in_1(t3_q), .out(src3b4));
  Decoder #(.Selector_Bits(5)) decoder_4 (
    .sel(waddr), .out_1(decoder_4_out_1), .out_2(decoder_4_out_2), .out_3(decoder_4_out_3),
    .out_4(decoder_4_out_4), .out_5(decoder_4_out_5), .out_6(decoder_4_out_6), .out_7(decoder_4_out_7),
    .out_8(decoder_4_out_8), .out_9(decoder_4_out_9), .out_10(decoder_4_out_10), .out_11(decoder_4_out_11),
    .out_12(decoder_4_out_12), .out_13(decoder_4_out_13), .out_14(decoder_4_out_14),
    .out_15(decoder_4_out_15), .out_16(decoder_4_out_16), .out_17(decoder_4_out_17),
    .out_18(decoder_4_out_18), .out_19(decoder_4_out_19), .out_20(decoder_4_out_20),
    .out_21(decoder_4_out_21), .out_22(decoder_4_out_22), .out_23(decoder_4_out_23),
    .out_28(decoder_4_out_28), .out_29(decoder_4_out_29), .out_30(decoder_4_out_30), .out_31(decoder_4_out_31));  // open: out_0, out_24, out_25, out_26, out_27
  Register #(.Bits(16)) t4 (.D(saved_temp_index_and_pointer), .C(s_t_i_p_clock), .en(decoder_4_out_5), .Q(t4_q));
  Multiplexer #(.Bits(16)) multiplexer_14 (.sel(src2r5), .in_0({16{1'b0}}), .in_1(t4_q), .out(src2b5));
  Multiplexer #(.Bits(16)) multiplexer_15 (.sel(src3r5), .in_0({16{1'b0}}), .in_1(t4_q), .out(src3b5));
  Multiplexer #(.Bits(16)) multiplexer_16 (.sel(src1r6), .in_0({16{1'b0}}), .in_1(t5_q), .out(src1b6));
  Multiplexer #(.Bits(16)) multiplexer_17 (.sel(src2r6), .in_0({16{1'b0}}), .in_1(t5_q), .out(src2b6));
  Register #(.Bits(16)) t5 (.D(saved_temp_index_and_pointer), .C(s_t_i_p_clock), .en(decoder_4_out_6), .Q(t5_q));
  Multiplexer #(.Bits(16)) multiplexer_18 (.sel(src1r7), .in_0({16{1'b0}}), .in_1(t6_q), .out(src1b7));
  Multiplexer #(.Bits(16)) multiplexer_19 (.sel(src3r6), .in_0({16{1'b0}}), .in_1(t5_q), .out(src3b6));
  Register #(.Bits(16)) t6 (.D(saved_temp_index_and_pointer), .C(s_t_i_p_clock), .en(decoder_4_out_7), .Q(t6_q));
  Multiplexer #(.Bits(16)) multiplexer_20 (.sel(src2r7), .in_0({16{1'b0}}), .in_1(t6_q), .out(src2b7));
  Multiplexer #(.Bits(16)) multiplexer_21 (.sel(src3r7), .in_0({16{1'b0}}), .in_1(t6_q), .out(src3b7));
  Multiplexer #(.Bits(16)) multiplexer_22 (.sel(src1r8), .in_0({16{1'b0}}), .in_1(t7_q), .out(src1b8));
  Multiplexer #(.Bits(16)) multiplexer_23 (.sel(src2r8), .in_0({16{1'b0}}), .in_1(t7_q), .out(src2b8));
  Register #(.Bits(16)) t7 (.D(saved_temp_index_and_pointer), .C(s_t_i_p_clock), .en(decoder_4_out_8), .Q(t7_q));
  Multiplexer #(.Bits(16)) multiplexer_24 (.sel(src1r9), .in_0({16{1'b0}}), .in_1(t8_q), .out(src1b9));
  Multiplexer #(.Bits(16)) multiplexer_25 (.sel(src3r8), .in_0({16{1'b0}}), .in_1(t7_q), .out(src3b8));
  Register #(.Bits(16)) t8 (.D(saved_temp_index_and_pointer), .C(s_t_i_p_clock), .en(decoder_4_out_9), .Q(t8_q));
  Multiplexer #(.Bits(16)) multiplexer_26 (.sel(src2r9), .in_0({16{1'b0}}), .in_1(t8_q), .out(src2b9));
  Multiplexer #(.Bits(16)) multiplexer_27 (.sel(src3r9), .in_0({16{1'b0}}), .in_1(t8_q), .out(src3b9));
  Multiplexer #(.Bits(16)) multiplexer_28 (.sel(src1r10), .in_0({16{1'b0}}), .in_1(t9_q), .out(src1b10));
  Multiplexer #(.Bits(16)) multiplexer_29 (.sel(src2r10), .in_0({16{1'b0}}), .in_1(t9_q), .out(src2b10));
  Register #(.Bits(16)) t9 (.D(saved_temp_index_and_pointer), .C(s_t_i_p_clock), .en(decoder_4_out_10), .Q(t9_q));
  Multiplexer #(.Bits(16)) multiplexer_30 (.sel(src1r11), .in_0({16{1'b0}}), .in_1(t10_q), .out(src1b11));
  Multiplexer #(.Bits(16)) multiplexer_31 (.sel(src3r10), .in_0({16{1'b0}}), .in_1(t9_q), .out(src3b10));
  Register #(.Bits(16)) t10 (.D(saved_temp_index_and_pointer), .C(s_t_i_p_clock), .en(decoder_4_out_11), .Q(t10_q));
  Multiplexer #(.Bits(16)) multiplexer_32 (.sel(src2r11), .in_0({16{1'b0}}), .in_1(t10_q), .out(src2b11));
  Multiplexer #(.Bits(16)) multiplexer_33 (.sel(src3r11), .in_0({16{1'b0}}), .in_1(t10_q), .out(src3b11));
  Multiplexer #(.Bits(16)) multiplexer_34 (.sel(src1r12), .in_0({16{1'b0}}), .in_1(t11_q), .out(src1b12));
  Multiplexer #(.Bits(16)) multiplexer_35 (.sel(src2r12), .in_0({16{1'b0}}), .in_1(t11_q), .out(src2b12));
  Register #(.Bits(16)) t11 (.D(saved_temp_index_and_pointer), .C(s_t_i_p_clock), .en(decoder_4_out_12), .Q(t11_q));
  Multiplexer #(.Bits(16)) multiplexer_36 (.sel(src1r13), .in_0({16{1'b0}}), .in_1(s0_q), .out(src1b13));
  Multiplexer #(.Bits(16)) multiplexer_37 (.sel(src3r12), .in_0({16{1'b0}}), .in_1(t11_q), .out(src3b12));
  Register #(.Bits(16)) s0 (.D(saved_temp_index_and_pointer), .C(s_t_i_p_clock), .en(decoder_4_out_13), .Q(s0_q));
  Multiplexer #(.Bits(16)) multiplexer_38 (.sel(src2r13), .in_0({16{1'b0}}), .in_1(s0_q), .out(src2b13));
  Multiplexer #(.Bits(16)) multiplexer_39 (.sel(src3r13), .in_0({16{1'b0}}), .in_1(s0_q), .out(src3b13));
  Multiplexer #(.Bits(16)) multiplexer_40 (.sel(src1r14), .in_0({16{1'b0}}), .in_1(s1_q), .out(src1b14));
  Multiplexer #(.Bits(16)) multiplexer_41 (.sel(src2r14), .in_0({16{1'b0}}), .in_1(s1_q), .out(src2b14));
  Register #(.Bits(16)) s1 (.D(saved_temp_index_and_pointer), .C(s_t_i_p_clock), .en(decoder_4_out_14), .Q(s1_q));
  Multiplexer #(.Bits(16)) multiplexer_42 (.sel(src1r15), .in_0({16{1'b0}}), .in_1(s2_q), .out(src1b15));
  Multiplexer #(.Bits(16)) multiplexer_43 (.sel(src3r14), .in_0({16{1'b0}}), .in_1(s1_q), .out(src3b14));
  Register #(.Bits(16)) s2 (.D(saved_temp_index_and_pointer), .C(s_t_i_p_clock), .en(decoder_4_out_15), .Q(s2_q));
  Multiplexer #(.Bits(16)) multiplexer_44 (.sel(src2r15), .in_0({16{1'b0}}), .in_1(s2_q), .out(src2b15));
  Multiplexer #(.Bits(16)) multiplexer_45 (.sel(src3r15), .in_0({16{1'b0}}), .in_1(s2_q), .out(src3b15));
  Multiplexer #(.Bits(16)) multiplexer_46 (.sel(src1r16), .in_0({16{1'b0}}), .in_1(s3_q), .out(src1b16));
  Multiplexer #(.Bits(16)) multiplexer_47 (.sel(src2r16), .in_0({16{1'b0}}), .in_1(s3_q), .out(src2b16));
  Register #(.Bits(16)) s3 (.D(saved_temp_index_and_pointer), .C(s_t_i_p_clock), .en(decoder_4_out_16), .Q(s3_q));
  Multiplexer #(.Bits(16)) multiplexer_48 (.sel(src1r17), .in_0({16{1'b0}}), .in_1(s4_q), .out(src1b17));
  Multiplexer #(.Bits(16)) multiplexer_49 (.sel(src3r16), .in_0({16{1'b0}}), .in_1(s3_q), .out(src3b16));
  Register #(.Bits(16)) s4 (.D(saved_temp_index_and_pointer), .C(s_t_i_p_clock), .en(decoder_4_out_17), .Q(s4_q));
  Multiplexer #(.Bits(16)) multiplexer_50 (.sel(src2r17), .in_0({16{1'b0}}), .in_1(s4_q), .out(src2b17));
  Multiplexer #(.Bits(16)) multiplexer_51 (.sel(src3r17), .in_0({16{1'b0}}), .in_1(s4_q), .out(src3b17));
  Multiplexer #(.Bits(16)) multiplexer_52 (.sel(src1r18), .in_0({16{1'b0}}), .in_1(s5_q), .out(src1b18));
  Multiplexer #(.Bits(16)) multiplexer_53 (.sel(src2r18), .in_0({16{1'b0}}), .in_1(s5_q), .out(src2b18));
  Register #(.Bits(16)) s5 (.D(saved_temp_index_and_pointer), .C(s_t_i_p_clock), .en(decoder_4_out_18), .Q(s5_q));
  Multiplexer #(.Bits(16)) multiplexer_54 (.sel(src1r19), .in_0({16{1'b0}}), .in_1(s6_q), .out(src1b19));
  Multiplexer #(.Bits(16)) multiplexer_55 (.sel(src3r18), .in_0({16{1'b0}}), .in_1(s5_q), .out(src3b18));
  Register #(.Bits(16)) s6 (.D(saved_temp_index_and_pointer), .C(s_t_i_p_clock), .en(decoder_4_out_19), .Q(s6_q));
  Multiplexer #(.Bits(16)) multiplexer_56 (.sel(src2r19), .in_0({16{1'b0}}), .in_1(s6_q), .out(src2b19));
  Multiplexer #(.Bits(16)) multiplexer_57 (.sel(src3r19), .in_0({16{1'b0}}), .in_1(s6_q), .out(src3b19));
  Multiplexer #(.Bits(16)) multiplexer_58 (.sel(src1r20), .in_0({16{1'b0}}), .in_1(s7_q), .out(src1b20));
  Multiplexer #(.Bits(16)) multiplexer_59 (.sel(src2r20), .in_0({16{1'b0}}), .in_1(s7_q), .out(src2b20));
  Register #(.Bits(16)) s7 (.D(saved_temp_index_and_pointer), .C(s_t_i_p_clock), .en(decoder_4_out_20), .Q(s7_q));
  Multiplexer #(.Bits(16)) multiplexer_60 (.sel(src1r21), .in_0({16{1'b0}}), .in_1(s8_q), .out(src1b21));
  Multiplexer #(.Bits(16)) multiplexer_61 (.sel(src3r20), .in_0({16{1'b0}}), .in_1(s7_q), .out(src3b20));
  Register #(.Bits(16)) s8 (.D(saved_temp_index_and_pointer), .C(s_t_i_p_clock), .en(decoder_4_out_21), .Q(s8_q));
  Multiplexer #(.Bits(16)) multiplexer_62 (.sel(src2r21), .in_0({16{1'b0}}), .in_1(s8_q), .out(src2b21));
  Multiplexer #(.Bits(16)) multiplexer_63 (.sel(src3r21), .in_0({16{1'b0}}), .in_1(s8_q), .out(src3b21));
  Multiplexer #(.Bits(16)) multiplexer_64 (.sel(src1r22), .in_0({16{1'b0}}), .in_1(ix_q), .out(src1b22));
  Multiplexer #(.Bits(16)) multiplexer_65 (.sel(src2r22), .in_0({16{1'b0}}), .in_1(ix_q), .out(src2b22));
  Register #(.Bits(16)) ix (.D(saved_temp_index_and_pointer), .C(s_t_i_p_clock), .en(decoder_4_out_22), .Q(ix_q));
  Multiplexer #(.Bits(16)) multiplexer_66 (.sel(src1r23), .in_0({16{1'b0}}), .in_1(iy_q), .out(src1b23));
  Multiplexer #(.Bits(16)) multiplexer_67 (.sel(src3r22), .in_0({16{1'b0}}), .in_1(ix_q), .out(src3b22));
  Register #(.Bits(16)) iy (.D(saved_temp_index_and_pointer), .C(s_t_i_p_clock), .en(decoder_4_out_23), .Q(iy_q));
  Multiplexer #(.Bits(16)) multiplexer_68 (.sel(src2r23), .in_0({16{1'b0}}), .in_1(iy_q), .out(src2b23));
  Multiplexer #(.Bits(16)) multiplexer_69 (.sel(src3r23), .in_0({16{1'b0}}), .in_1(iy_q), .out(src3b23));
  Multiplexer #(.Bits(16)) multiplexer_70 (.sel(src1r28), .in_0({16{1'b0}}), .in_1(fp_q), .out(src1b28));
  Multiplexer #(.Bits(16)) multiplexer_71 (.sel(src2r28), .in_0({16{1'b0}}), .in_1(fp_q), .out(src2b28));
  Register #(.Bits(16)) fp (.D(saved_temp_index_and_pointer), .C(s_t_i_p_clock), .en(decoder_4_out_28), .Q(fp_q));
  Multiplexer #(.Bits(16)) multiplexer_72 (.sel(src1r29), .in_0({16{1'b0}}), .in_1(gp_q), .out(src1b29));
  Multiplexer #(.Bits(16)) multiplexer_73 (.sel(src3r28), .in_0({16{1'b0}}), .in_1(fp_q), .out(src3b28));
  Register #(.Bits(16)) gp (.D(saved_temp_index_and_pointer), .C(s_t_i_p_clock), .en(decoder_4_out_29), .Q(gp_q));
  Multiplexer #(.Bits(16)) multiplexer_74 (.sel(src2r29), .in_0({16{1'b0}}), .in_1(gp_q), .out(src2b29));
  Multiplexer #(.Bits(16)) multiplexer_75 (.sel(src3r29), .in_0({16{1'b0}}), .in_1(gp_q), .out(src3b29));
  Multiplexer #(.Bits(16)) multiplexer_76 (.sel(src1r30), .in_0({16{1'b0}}), .in_1(sp_q), .out(src1b30));
  Multiplexer #(.Bits(16)) multiplexer_77 (.sel(src2r30), .in_0({16{1'b0}}), .in_1(sp_q), .out(src2b30));
  Register #(.Bits(16)) sp (.D(saved_temp_index_and_pointer), .C(s_t_i_p_clock), .en(decoder_4_out_30), .Q(sp_q));
  Multiplexer #(.Bits(16)) multiplexer_78 (.sel(src1r31), .in_0({16{1'b0}}), .in_1(ra_q), .out(src1b31));
  Multiplexer #(.Bits(16)) multiplexer_79 (.sel(src3r30), .in_0({16{1'b0}}), .in_1(sp_q), .out(src3b30));
  Register #(.Bits(16)) ra (.D(saved_temp_index_and_pointer), .C(s_t_i_p_clock), .en(decoder_4_out_31), .Q(ra_q));
  Multiplexer #(.Bits(16)) multiplexer_80 (.sel(src2r31), .in_0({16{1'b0}}), .in_1(ra_q), .out(src2b31));
  Multiplexer #(.Bits(16)) multiplexer_81 (.sel(src3r31), .in_0({16{1'b0}}), .in_1(ra_q), .out(src3b31));
  Register #(.Bits(16)) mh (.D(mhdata), .C(muldivclock), .en(muldivclock), .Q(mh_q));
  Multiplexer #(.Bits(16)) multiplexer_82 (.sel(src1r24), .in_0({16{1'b0}}), .in_1(mh_q), .out(src1b24));
  Multiplexer #(.Bits(16)) multiplexer_83 (.sel(src2r24), .in_0({16{1'b0}}), .in_1(mh_q), .out(src2b24));
  Multiplexer #(.Bits(16)) multiplexer_84 (.sel(src1r25), .in_0({16{1'b0}}), .in_1(ml_q), .out(src1b25));
  Multiplexer #(.Bits(16)) multiplexer_85 (.sel(src3r24), .in_0({16{1'b0}}), .in_1(mh_q), .out(src3b24));
  Register #(.Bits(16)) ml (.D(mldata), .C(muldivclock), .en(muldivclock), .Q(ml_q));
  Multiplexer #(.Bits(16)) multiplexer_86 (.sel(src2r25), .in_0({16{1'b0}}), .in_1(ml_q), .out(src2b25));
  Multiplexer #(.Bits(16)) multiplexer_87 (.sel(src3r25), .in_0({16{1'b0}}), .in_1(ml_q), .out(src3b25));
  Register #(.Bits(16)) dq (.D(dqdata), .C(muldivclock), .en(muldivclock), .Q(dq_q));
  Multiplexer #(.Bits(16)) multiplexer_88 (.sel(src1r26), .in_0({16{1'b0}}), .in_1(dq_q), .out(src1b26));
  Multiplexer #(.Bits(16)) multiplexer_89 (.sel(src2r26), .in_0({16{1'b0}}), .in_1(dq_q), .out(src2b26));
  Multiplexer #(.Bits(16)) multiplexer_90 (.sel(src1r27), .in_0({16{1'b0}}), .in_1(dr_q), .out(src1b27));
  Multiplexer #(.Bits(16)) multiplexer_91 (.sel(src3r26), .in_0({16{1'b0}}), .in_1(dq_q), .out(src3b26));
  Register #(.Bits(16)) dr (.D(drdata), .C(muldivclock), .en(muldivclock), .Q(dr_q));
  Multiplexer #(.Bits(16)) multiplexer_92 (.sel(src2r27), .in_0({16{1'b0}}), .in_1(dr_q), .out(src2b27));
  Multiplexer #(.Bits(16)) multiplexer_93 (.sel(src3r27), .in_0({16{1'b0}}), .in_1(dr_q), .out(src3b27));

  // Notes on the sheet:
  //   register map		
  //   zero register	r0	0
  //   temp 0	t0	1
  //   temp 1	t1	2
  //   temp 2	t2	3
  //   temp 3	t3	4
  //   temp 4	t4	5
  //   temp 5	t5	6
  //   temp 6	t6	7
  //   temp 7	t7	8
  //   temp 8	t8	9
  //   temp 9	t9	10
  //   temp 10	t10	11
  //   temp 11	t11	12
  //   save 0	s0	13
  //   save 1	s1	14
  //   save 2	s2	15
  //   save 3	s3	16
  //   save 4	s4	17
  //   save 5	s5	18
  //   save 6	s6	19
  //   save 7	s7	20
  //   save 8	s8	21
  //   Index X	IX	22
  //   Index Y	IY	23
  //   mult low	ML	24
  //   mult hi	MH	25
  //   divider remainder	DR	26
  //   divider quotient	DQ	27
  //   frame pointer	fp	28
  //   global pointer	gp	29
  //   stack pointer	sp	30
  //   return address	ra	31
endmodule
